// Digital circuit ABS16.dig as structural Verilog
module ABS16 (
  input  [15:0] R,
  input  S,
  output [15:0] MAG
);

  wire [15:0] xor_1_out;

  assign xor_1_out = R ^ {16{S}};  // XOr xor_1, 16 bits wide
  ADD16 add16_1 (.A(xor_1_out), .B({16{1'b0}}), .CIN(S), .SUM(MAG));  // open: COUT
endmodule
