// Digital circuit ADD16.dig as structural Verilog
module ADD16 (
  input  [15:0] A,
  input  [15:0] B,
  input  CIN,
  output COUT,
  output [15:0] SUM
);

  wire add4_1_cout, add4_2_cout, add4_3_cout;

  ADD4 add4_1 (.A(A[3:0]), .B(B[3:0]), .CIN(CIN), .COUT(add4_1_cout), .SUM(SUM[3:0]));
  ADD4 add4_2 (.A(A[7:4]), .B(B[7:4]), .CIN(add4_1_cout), .COUT(add4_2_cout), .SUM(SUM[7:4]));
  ADD4 add4_3 (.A(A[11:8]), .B(B[11:8]), .CIN(add4_2_cout), .COUT(add4_3_cout), .SUM(SUM[11:8]));
  ADD4 add4_4 (.A(A[15:12]), .B(B[15:12]), .CIN(add4_3_cout), .COUT(COUT), .SUM(SUM[15:12]));
endmodule
