// Digital circuit ADD4.dig as structural Verilog
module ADD4 (
  input  [3:0] A,
  input  [3:0] B,
  input  CIN,
  output COUT,
  output [3:0] SUM
);

  wire fa_1_p5, fa_2_p5, fa_3_p5;

  // FA fa_1: pin names not known; wires that end beside it: A[0], B[0], CIN, SUM[0], fa_1_p5
  // FA fa_2: pin names not known; wires that end beside it: A[1], B[1], fa_1_p5, SUM[1], fa_2_p5
  // FA fa_3: pin names not known; wires that end beside it: A[2], B[2], fa_2_p5, SUM[2], fa_3_p5
  // FA fa_4: pin names not known; wires that end beside it: A[3], B[3], fa_3_p5, SUM[3], COUT
endmodule
