// Digital circuit ADDSUB16.dig as structural Verilog
module ADDSUB16 (
  input  [15:0] A,
  input  [15:0] B,
  input  M,
  output [15:0] R,
  output COUT
);

  wire [15:0] xor_1_out;

  assign xor_1_out = B ^ {16{M}};  // XOr xor_1, 16 bits wide
  ADD16 add16_1 (.A(A), .B(xor_1_out), .CIN(M), .COUT(COUT), .SUM(R));
endmodule
