// Digital circuit ALU16.dig as structural Verilog
module ALU16 (
  input  [15:0] A,
  input  [15:0] B,
  input  [1:0] OP,
  output [15:0] R,
  output COUT
);

  wire and_1_out, not_1_out;
  wire [15:0] addsub16_1_r, logic16_1_and_r, logic16_1_or_r;

  not not_1 (not_1_out, OP[1]);
  and and_1 (and_1_out, OP[0], not_1_out);
  ADDSUB16 addsub16_1 (.A(A), .B(B), .M(and_1_out), .R(addsub16_1_r), .COUT(COUT));
  LOGIC16 logic16_1 (.A(A), .B(B), .AND_R(logic16_1_and_r), .OR_R(logic16_1_or_r));
  Multiplexer #(.Bits(16), .Selector_Bits(2)) multiplexer_1 (
    .sel(OP), .in_0(addsub16_1_r), .in_1(addsub16_1_r), .in_2(logic16_1_and_r), .in_3(logic16_1_or_r), .out(R));
endmodule
