// Digital circuit FA.dig as structural Verilog
module FA (
  input  [3:0] A,
  input  [3:0] B,
  input  CIN,
  output [3:0] SUM,
  output COUT
);

  wire and_1_out, and_2_out, and_3_out, or_1_out, xor_1_out;

  xor xor_1 (xor_1_out, A[0], B[0]);
  xor xor_2 (SUM[0], xor_1_out, CIN);
  and and_1 (and_1_out, A[0], B[0]);
  and and_2 (and_2_out, A[0], CIN);
  and and_3 (and_3_out, B[0], CIN);
  or or_1 (or_1_out, and_1_out, and_2_out);
  or or_2 (COUT, or_1_out, and_3_out);
  // Pins of 1 and 4 bits meet at A
  // Pins of 1 and 4 bits meet at B
  // Pins of 1 and 4 bits meet at SUM
endmodule
