// Digital circuit LOGIC16.dig as structural Verilog
module LOGIC16 (
  input  [15:0] A,
  input  [15:0] B,
  output [15:0] AND_R,
  output [15:0] OR_R
);

  assign AND_R = A & B;  // And and_1, 16 bits wide
  assign OR_R = A | B;  // Or or_1, 16 bits wide
endmodule
