// Digital circuit MAIN.dig as structural Verilog
module MAIN (
  input  [15:0] A,
  input  [15:0] B,
  input  [1:0] OP
);

  wire opdisp_1_a_c_f, opdisp_1_b__e, opdisp_1_d, opdisp_1_g, sign_1_s, signdisp_1_a, signdisp_1_b,
       signdisp_1_c, signdisp_1_d, signdisp_1_e, signdisp_1_f, signdisp_1_g;
  wire [3:0] abs16_1_mag, abs16_1_mag_2;
  wire [15:0] alu16_1_r;
  wire [15:8] abs16_1_mag_3;

  ALU16 alu16_1 (.A(A), .B(B), .OP(OP), .R(alu16_1_r));  // open: COUT
  SIGN sign_1 (.R(alu16_1_r), .OP(OP), .S(sign_1_s));
  ABS16 abs16_1 (.R(alu16_1_r), .S(sign_1_s), .MAG({abs16_1_mag_3, abs16_1_mag_2, abs16_1_mag}));
  OPDISP opdisp_1 (.OP(OP), .a_c_f(opdisp_1_a_c_f), .b__e(opdisp_1_b__e), .d(opdisp_1_d), .g(opdisp_1_g));
  Seven_Seg_Hex seven_seg_hex_1 (.d(abs16_1_mag_3[15:12]), .dp(1'b0));
  SIGNDISP signdisp_1 (
    .S(sign_1_s), .c(signdisp_1_c), .d(signdisp_1_d), .e(signdisp_1_e), .f(signdisp_1_f), .b(signdisp_1_b),
    .a(signdisp_1_a), .g(signdisp_1_g));
  Seven_Seg seven_seg_1 (
    .a(opdisp_1_a_c_f), .b(opdisp_1_b__e), .c(opdisp_1_a_c_f), .d(opdisp_1_d), .e(opdisp_1_b__e),
    .f(opdisp_1_a_c_f), .g(opdisp_1_g), .dp(1'b0));
  Seven_Seg_Hex seven_seg_hex_2 (.d(abs16_1_mag_3[11:8]), .dp(1'b0));
  Seven_Seg seven_seg_2 (
    .a(signdisp_1_a), .b(signdisp_1_b), .c(signdisp_1_c), .d(signdisp_1_d), .e(signdisp_1_e),
    .f(signdisp_1_f), .g(signdisp_1_g), .dp(1'b0));
  Seven_Seg_Hex seven_seg_hex_3 (.d(abs16_1_mag_2), .dp(1'b0));
  Seven_Seg_Hex seven_seg_hex_4 (.d(abs16_1_mag), .dp(1'b0));
endmodule
