// Digital circuit OPDISP.dig as structural Verilog
module OPDISP (
  input  [1:0] OP,
  output a_c_f,
  output b__e,
  output d,
  output g
);

  wire not_1_out;

  or or_1 (b__e, not_1_out, OP[1]);
  not not_1 (not_1_out, OP[0]);
  and and_1 (d, OP[0], OP[1]);
  nand nand_1 (g, OP[0], OP[1]);

  assign a_c_f = OP[1];
endmodule
