// Digital circuit SIGN.dig as structural Verilog
module SIGN (
  input  [15:0] R,
  input  [1:0] OP,
  output S
);

  wire not_1_out;

  not not_1 (not_1_out, OP[1]);
  and and_1 (S, R[15], not_1_out);
endmodule
